// Logisim project computer.circ as structural Verilog: 4 circuits, main circuit main
module main (
  input  [7:0] input_pins,
  output [7:0] output_pins
);

  wire AI, alu_c_ezero, alu_c_gzero, ALUO, AO, CI, clock_1_out, CO, DI, DO, IO, IRI, JMPO, MARI, OI,
       pc_low_carry, PCC, PCHI, RAMI, RAMO, RESET, ROMO, ROMOT, STOPPCC;
  wire [2:0] cu_c_outflag;
  wire [3:0] cu_c_inflag;
  wire [7:0] alu_c_aluout, and_1_out, and_2_out, areg_q, bit_extender_1_out, bit_extender_2_out, CINS,
       creg_q, dreg_q, ireg_q, mar_q, multiplexer_1_out, or_2_out, pc_rom_data, ram_c_dout;
  wire [15:0] PCIN, PCOUT;

  Clock clock_1 (.out(clock_1_out));
  Counter pc_low (
    .clr(RESET), .load(PCHI), .up(1'b1), .count(PCC), .clk(clock_1_out), .D(PCIN[7:0]), .carry(pc_low_carry),
    .Q(PCOUT[7:0]));
  ROM #(.addrWidth(16)) pc_rom (.addr(PCOUT), .data(pc_rom_data));
  Register mar (.D(or_2_out), .en(MARI), .clk(clock_1_out), .Q(mar_q), .clr(RESET));
  cu cu_c (
    .IRIN(or_2_out), .IRI_IN(IRI), .CLK(clock_1_out), .RESET(RESET), .STOPPCC(STOPPCC), .CUOUT(CINS),
    .INFLAG(cu_c_inflag), .OUTFLAG(cu_c_outflag), .PCC(PCC), .IRI_OUT(IRI));
  Decoder #(.select(3), .enable("false")) decoder_1 (
    .out1(IO), .out2(AO), .out3(CO), .out4(DO), .out5(ROMOT), .out6(RAMO), .out7(JMPO), .sel(cu_c_outflag));  // open: out0
  RAM #(.databus("bibus")) ram_c (
    .addr(mar_q), .we(RAMI), .oe(RAMO), .clk(clock_1_out), .din(or_2_out), .dout(ram_c_dout));
  or or_1 (ROMO, IRI, ROMOT, JMPO);
  Counter pc_high (
    .clr(RESET), .load(PCHI), .up(1'b1), .clk(pc_low_carry), .D(PCIN[15:8]), .Q(PCOUT[15:8]));  // open: count, carry
  Button reset_button (.out(RESET));
  assign and_1_out = pc_rom_data & bit_extender_1_out;  // AND_Gate and_1, 8 bits wide
  assign bit_extender_1_out = {{7{ROMO}}, ROMO};  // Bit_Extender bit_extender_1
  Decoder #(.select(4), .enable("false")) decoder_2 (
    .out1(OI), .out2(RAMI), .out3(MARI), .out4(AI), .out5(CI), .out6(DI), .sel(cu_c_inflag));  // open: out0, out7, out8, out9, out10, out11, out12, out13, out14, out15
  assign or_2_out = ram_c_dout | and_1_out | alu_c_aluout | and_2_out;  // OR_Gate or_2, 8 bits wide
  Register areg (.D(or_2_out), .en(AI), .clk(clock_1_out), .Q(areg_q), .clr(RESET));
  Register creg (.D(or_2_out), .en(CI), .clk(clock_1_out), .Q(creg_q), .clr(RESET));
  Register dreg (.D(or_2_out), .en(DI), .clk(clock_1_out), .Q(dreg_q), .clr(RESET));
  Register oreg (.D(or_2_out), .en(OI), .clk(clock_1_out), .Q(output_pins), .clr(RESET));
  Register ireg (.D(input_pins), .en(1'b1), .clk(clock_1_out), .Q(ireg_q), .clr(RESET));
  assign and_2_out = ireg_q & bit_extender_2_out;  // AND_Gate and_2, 8 bits wide
  or or_3 (ALUO, JMPO, AO, CO, DO);
  alu alu_c (
    .A(areg_q), .B(multiplexer_1_out), .CLK(clock_1_out), .RESET(RESET), .CINS(CINS), .OE(ALUO),
    .GZERO(alu_c_gzero), .EZERO(alu_c_ezero), .ALUOUT(alu_c_aluout));
  Multiplexer #(.width(8), .enable("false")) multiplexer_1 (
    .in0(creg_q), .in1(dreg_q), .out(multiplexer_1_out), .sel(DO));
  assign bit_extender_2_out = {{7{IO}}, IO};  // Bit_Extender bit_extender_2
  jmp jmp_c (
    .JMPINS(CINS), .JMPO(JMPO), .GZERO(alu_c_gzero), .EZERO(alu_c_ezero), .PCIN(PCIN), .DATABUS(or_2_out),
    .PCO(PCHI), .PCOUT(PCIN));
  D_Flip_Flop #(.trigger("falling")) d_ff_1 (.D(PCHI), .clk(clock_1_out), .Q(STOPPCC));  // open: Qn, preset, reset

  // Other names for the same wires on the sheet: DOO = DO; PCLI = PCHI

  // Notes on the sheet:
  //   contents of pc_rom (hex, n*v repeats v):
  //   60 10 61 12 4d 90 20
  //   Output termination
  //   Data bus
endmodule

module alu (
  input  [7:0] A,
  input  [7:0] B,
  input  CLK,
  input  RESET,
  input  [7:0] CINS,
  input  OE,
  output GZERO,
  output EZERO,
  output [7:0] ALUOUT
);

  wire adder_1_cout, and_5_out, CARRY, d_ff_1_q, IA, IB, IO, ZA, ZB;
  wire [1:0] CSELECT;
  wire [7:0] adder_1_out, and_1_out, and_2_out, and_3_out, and_4_out, multiplexer_1_out, shifter_1_out,
       shifter_2_out, xor_1_out, xor_2_out;

  assign and_1_out = ~{8{ZA}} & A;  // AND_Gate and_1, 8 bits wide
  assign and_2_out = B & ~{8{ZB}};  // AND_Gate and_2, 8 bits wide
  assign xor_1_out = {8{IA}} ^ and_1_out;  // XOR_Gate xor_1, 8 bits wide
  Adder adder_1 (.a(xor_2_out), .b(xor_1_out), .out(adder_1_out), .cin(and_5_out), .cout(adder_1_cout));
  assign and_3_out = xor_2_out & xor_1_out;  // AND_Gate and_3, 8 bits wide
  Shifter #(.shift("lr")) shifter_1 (.in(xor_2_out), .\dist (xor_1_out[2:0]), .out(shifter_1_out));
  Shifter shifter_2 (.in(xor_2_out), .\dist (xor_1_out[2:0]), .out(shifter_2_out));
  D_Flip_Flop #(.trigger("falling")) d_ff_1 (
    .D(adder_1_cout), .clk(CLK), .Q(d_ff_1_q), .reset(RESET));  // open: Qn, preset
  ROM alu_rom (.addr(and_4_out), .data({CSELECT, CARRY, IO, IB, ZB, IA, ZA}));
  assign and_4_out = CINS & {8{OE}};  // AND_Gate and_4, 8 bits wide
  assign xor_2_out = and_2_out ^ {8{IB}};  // XOR_Gate xor_2, 8 bits wide
  Multiplexer #(.select(2), .width(8), .enable("false")) multiplexer_1 (
    .in0(adder_1_out), .in1(and_3_out), .in2(shifter_1_out), .in3(shifter_2_out), .out(multiplexer_1_out),
    .sel(CSELECT));
  and and_5 (and_5_out, d_ff_1_q, CARRY);
  assign ALUOUT = {8{IO}} ^ multiplexer_1_out;  // XOR_Gate xor_3, 8 bits wide
  or or_1 (GZERO, ALUOUT[7], ALUOUT[6], ALUOUT[5], ALUOUT[4], ALUOUT[3], ALUOUT[2], ALUOUT[1], ALUOUT[0]);
  nor nor_1 (EZERO, ALUOUT[7], ALUOUT[6], ALUOUT[5], ALUOUT[4], ALUOUT[3], ALUOUT[2], ALUOUT[1], ALUOUT[0]);

  // Notes on the sheet:
  //   contents of alu_rom (hex, n*v repeats v):
  //   16*5 4 4 4*1 43*5 1f 7 4 1 14 11 1c 13 1e 1b c 3 0 12 18 80 96 20 40 28*5 4 1 1 4 4 1 26*5 4 1 1
  //   109*5
endmodule

module cu (
  input  [7:0] IRIN,
  input  IRI_IN,
  input  CLK,
  input  RESET,
  input  STOPPCC,
  output [7:0] CUOUT,
  output [3:0] INFLAG,
  output [2:0] OUTFLAG,
  output PCC,
  output IRI_OUT
);

  wire and_2_out, decoder_1_out1, decoder_1_out2, decoder_1_out3, or_1_out, undriven;
  wire [1:0] CUCTR_q;
  wire [6:0] bit_extender_1_out, cu_rom_data;

  Counter #(.width(2), .max('h3), .trigger("falling")) CUCTR (
    .clr(RESET), .clk(CLK), .Q(CUCTR_q));  // open: load, up, count, D, carry
  Register register_1 (.D(IRIN), .en(IRI_IN), .clk(CLK), .Q(CUOUT), .clr(RESET));
  ROM #(.dataWidth(7)) cu_rom (.addr(CUOUT), .data(cu_rom_data));
  ROM #(.addrWidth(4), .dataWidth(1)) ins_rom (.addr(CUOUT[7:4]));  // open: data
  Decoder #(.select(2), .enable("false")) decoder_1 (
    .out0(IRI_OUT), .out1(decoder_1_out1), .out2(decoder_1_out2), .out3(decoder_1_out3), .sel(CUCTR_q));
  assign {OUTFLAG, INFLAG} = cu_rom_data & bit_extender_1_out;  // AND_Gate and_1, 7 bits wide
  assign bit_extender_1_out = {{6{decoder_1_out2}}, decoder_1_out2};  // Bit_Extender bit_extender_1
  and and_2 (and_2_out, undriven, decoder_1_out1);
  or or_1 (or_1_out, and_2_out, decoder_1_out3);
  and and_3 (PCC, ~STOPPCC, or_1_out);  // AND_Gate

  // Other names for the same wires on the sheet: INSTYPE[3:0] = CUOUT[7:4]

  // Notes on the sheet:
  //   contents of cu_rom (hex, n*v repeats v):
  //   16*0 25 26 34 26 44 45 10*0 15*70 0 15*70 0 32*34 54 55 56 64 65 66 10*0 22 32 42 23 33 43 10*0 14
  //   15 16 13*0 21 31 41
  //   contents of ins_rom (hex, n*v repeats v):
  //   0 0 1 0 0 0 1
  //   after the first clock cycle
  //   If load or jmp instruction, we should activate PC
endmodule

module jmp (
  input  [7:0] JMPINS,
  input  JMPO,
  input  GZERO,
  input  EZERO,
  input  [15:0] PCIN,
  input  [7:0] DATABUS,
  output PCO,
  output [15:0] PCOUT
);

  wire and_2_out, and_3_out, and_4_out, and_5_out, or_1_out, or_2_out;
  wire [6:0] rom_1_data;
  wire [7:0] and_1_out, bit_extender_1_out;
  wire [15:0] adder_1_out, bit_extender_2_out;

  ROM #(.dataWidth(7)) rom_1 (.addr(and_1_out), .data(rom_1_data));
  assign and_1_out = JMPINS & bit_extender_1_out;  // AND_Gate and_1, 8 bits wide
  assign bit_extender_1_out = {{7{JMPO}}, JMPO};  // Bit_Extender bit_extender_1
  and and_2 (and_2_out, ~GZERO, rom_1_data[0]);  // AND_Gate
  and and_3 (and_3_out, GZERO, rom_1_data[1]);
  and and_4 (and_4_out, ~EZERO, rom_1_data[3]);  // AND_Gate
  and and_5 (and_5_out, EZERO, rom_1_data[4]);
  Adder #(.width(16)) adder_1 (.a(PCIN), .b(bit_extender_2_out), .out(adder_1_out));  // open: cin, cout
  assign bit_extender_2_out = {{8{1'b0}}, DATABUS};  // Bit_Extender bit_extender_2
  or or_1 (or_1_out, and_2_out, rom_1_data[2], and_3_out);
  and and_6 (PCO, or_1_out, or_2_out);
  or or_2 (or_2_out, and_4_out, rom_1_data[5], and_5_out);
  Multiplexer #(.width(16)) multiplexer_1 (
    .in0(bit_extender_2_out), .in1(adder_1_out), .out(PCOUT), .sel(rom_1_data[6]), .en(PCO));

  // Notes on the sheet:
  //   contents of rom_1 (hex, n*v repeats v):
  //   32*0 24 21 9 14 a 22 21 9 14 a 22 21 9 14 a 22 64 61 49 54 4a 62 61 49 54 4a 62 61 49 54 4a 62
endmodule
