// Logisim project computer_fpga.circ as structural Verilog: 6 circuits, main circuit main
module main (
  input  clk,
  input  [7:0] input_pins,
  output [7:0] output_pins
);

  wire AI, alu_c_carryout, alu_c_cmpo, alu_c_overout, ALUO, and_1_out, AO, CI, cmp_c_cflago, cmp_c_oflago,
       cmp_c_sflago, cmp_c_zflago, CO, DI, DipSwitch_1_sw1, DO, IO, IRI, JMPO, MARI, not_1_out, OI,
       pc_low_carry, PCC, PCHI, RAMI, RAMO, RESET, ROMO, ROMOT;
  wire [2:0] cu_c_outflag;
  wire [3:0] cu_c_inflag;
  wire [7:0] alu_c_aluout, and_2_out, and_3_out, and_4_out, areg_q, bit_extender_1_out, bit_extender_2_out,
       bit_extender_3_out, CINS, creg_q, demultiplexer_1_out0, demultiplexer_1_out1, dreg_q, ireg_q, mar_q,
       multiplexer_1_out, or_3_out, pc_rom_data, ram_c_dout, undriven;
  wire [15:0] or_1_out, pc_low_q, PCIN;

  DipSwitch #(.number(2)) DipSwitch_1 (.sw1(DipSwitch_1_sw1));  // open: sw2
  Demultiplexer #(.width(8)) demultiplexer_1 (
    .out0(demultiplexer_1_out0), .out1(demultiplexer_1_out1), .in(undriven), .sel(DipSwitch_1_sw1));
  // DipSwitch DipSwitch_2: pin names not known
  assign or_1_out = PCIN | {demultiplexer_1_out1, demultiplexer_1_out0};  // OR_Gate or_1, 16 bits wide
  Counter pc_low (
    .clr(RESET), .load(PCHI), .up(1'b1), .count(PCC), .clk(clk), .D(or_1_out[7:0]), .carry(pc_low_carry),
    .Q(pc_low_q[7:0]));
  ROM #(.addrWidth(16)) pc_rom (.addr(pc_low_q), .data(pc_rom_data));
  Register mar (.D(or_3_out), .en(MARI), .clk(clk), .Q(mar_q), .clr(RESET));
  Button reset_button (.out(RESET));
  not not_1 (not_1_out, clk);
  cu cu_c (
    .IRIN(or_3_out), .IRI_IN(IRI), .CLK(clk), .RESET(RESET), .CUOUT(CINS), .INFLAG(cu_c_inflag),
    .OUTFLAG(cu_c_outflag), .PCC(PCC), .IRI_OUT(IRI));
  RAM ram_c (.addr(mar_q), .we(RAMI), .oe(1'b1), .clk(not_1_out), .din(or_3_out), .dout(ram_c_dout));
  Decoder #(.enable("false"), .select(3)) decoder_1 (
    .out1(IO), .out2(AO), .out3(CO), .out4(DO), .out5(ROMOT), .out6(RAMO), .out7(JMPO), .sel(cu_c_outflag));  // open: out0
  Counter pc_high (
    .clr(RESET), .load(PCHI), .up(1'b1), .count(and_1_out), .clk(clk), .D(or_1_out[15:8]), .Q(pc_low_q[15:8]));  // open: carry
  and and_1 (and_1_out, pc_low_carry, PCC);
  or or_2 (ROMO, PCC, ROMOT);
  assign bit_extender_1_out = {{7{ROMO}}, ROMO};  // Bit_Extender bit_extender_1
  assign bit_extender_2_out = {{7{RAMO}}, RAMO};  // Bit_Extender bit_extender_2
  assign and_2_out = pc_rom_data & bit_extender_1_out;  // AND_Gate and_2, 8 bits wide
  assign and_3_out = bit_extender_2_out & ram_c_dout;  // AND_Gate and_3, 8 bits wide
  assign or_3_out = and_3_out | and_2_out | alu_c_aluout | and_4_out;  // OR_Gate or_3, 8 bits wide
  Decoder #(.enable("false"), .select(4)) decoder_2 (
    .out1(OI), .out2(RAMI), .out3(MARI), .out4(AI), .out5(CI), .out6(DI), .sel(cu_c_inflag));  // open: out0, out7, out8, out9, out10, out11, out12, out13, out14, out15
  Register areg (.D(or_3_out), .en(AI), .clk(clk), .Q(areg_q), .clr(RESET));
  Register creg (.D(or_3_out), .en(CI), .clk(clk), .Q(creg_q), .clr(RESET));
  Register dreg (.D(or_3_out), .en(DI), .clk(clk), .Q(dreg_q), .clr(RESET));
  Register oreg (.D(or_3_out), .en(OI), .clk(clk), .Q(output_pins), .clr(RESET));
  Register ireg (.D(input_pins), .en(1'b1), .clk(clk), .Q(ireg_q), .clr(RESET));
  or or_4 (ALUO, AO, CO, DO);
  assign and_4_out = ireg_q & bit_extender_3_out;  // AND_Gate and_4, 8 bits wide
  assign bit_extender_3_out = {{7{IO}}, IO};  // Bit_Extender bit_extender_3
  alu alu_c (
    .A(areg_q), .B(multiplexer_1_out), .CARRYIN(cmp_c_cflago), .OE(ALUO), .CINS(CINS), .ALUOUT(alu_c_aluout),
    .OVEROUT(alu_c_overout), .CARRYOUT(alu_c_carryout), .CMPO(alu_c_cmpo));
  Multiplexer #(.width(8)) multiplexer_1 (.in0(creg_q), .in1(dreg_q), .out(multiplexer_1_out), .sel(DO));
  cmp cmp_c (
    .CMPIN(alu_c_aluout), .OVERFLOW(alu_c_overout), .CARRY(alu_c_carryout), .OE(alu_c_cmpo), .CLK(clk),
    .RESET(RESET), .ZFLAGO(cmp_c_zflago), .OFLAGO(cmp_c_oflago), .CFLAGO(cmp_c_cflago), .SFLAGO(cmp_c_sflago));
  jmp jmp_c (
    .JMPINS(CINS), .OE(JMPO), .ZIN(cmp_c_zflago), .OIN(cmp_c_oflago), .CIN(cmp_c_cflago), .SIN(cmp_c_sflago),
    .PCIN(PCIN), .DATABUS(or_3_out), .CLK(clk), .RESET(RESET), .PCOE(PCHI), .PCOUT(PCIN));

  // Other names for the same wires on the sheet: DOO = DO; PCLI = PCHI

  // Notes on the sheet:
  //   contents of pc_rom (hex, n*v repeats v):
  //   70 1 71 0 11 5d 33 0 0 b0 15 36 0 4
  //   Output termination
  //   Data bus
endmodule

module alu (
  input  [7:0] A,
  input  [7:0] B,
  input  CARRYIN,
  input  OE,
  input  [7:0] CINS,
  output [7:0] ALUOUT,
  output OVEROUT,
  output CARRYOUT,
  output CMPO
);

  wire and_2_out, and_5_out, and_6_out, CARRY, IA, IB, IO, ZA, ZB;
  wire [1:0] CSELECT;
  wire [2:0] xor_2_out;
  wire [7:0] adder_1_out, and_1_out, and_3_out, and_4_out, bit_extender_1_out, multiplexer_1_out,
       shifter_1_out, shifter_2_out, xor_1_out, xor_3_out;
  wire [7:3] xor_2_out_2;
  wire [8:8] alu_rom_data;

  assign and_1_out = ~{8{ZA}} & A;  // AND_Gate and_1, 8 bits wide
  assign xor_1_out = {8{IA}} ^ and_1_out;  // XOR_Gate xor_1, 8 bits wide
  and and_2 (and_2_out, CARRYIN, CARRY);
  ROM #(.dataWidth(9)) alu_rom (.addr(CINS), .data({alu_rom_data[8], CSELECT, CARRY, IO, IB, ZB, IA, ZA}));
  assign and_3_out = B & ~{8{ZB}};  // AND_Gate and_3, 8 bits wide
  assign {xor_2_out_2, xor_2_out} = and_3_out ^ {8{IB}};  // XOR_Gate xor_2, 8 bits wide
  Adder adder_1 (.a({xor_2_out_2, xor_2_out}), .b(xor_1_out), .out(adder_1_out), .cin(and_2_out), .cout(CARRYOUT));
  assign and_4_out = {xor_2_out_2, xor_2_out} & xor_1_out;  // AND_Gate and_4, 8 bits wide
  Shifter #(.shift("lr")) shifter_1 (.in(xor_1_out), .\dist (xor_2_out), .out(shifter_1_out));
  Shifter shifter_2 (.in(xor_1_out), .\dist (xor_2_out), .out(shifter_2_out));
  Multiplexer #(.select(2), .width(8)) multiplexer_1 (
    .in0(adder_1_out), .in1(and_4_out), .in2(shifter_1_out), .in3(shifter_2_out), .out(multiplexer_1_out),
    .sel(CSELECT));
  and and_5 (and_5_out, xor_2_out_2[7], ~xor_3_out[7], xor_1_out[7]);  // AND_Gate
  or or_1 (OVEROUT, and_5_out, and_6_out);
  and and_6 (and_6_out, ~xor_2_out_2[7], xor_3_out[7], ~xor_1_out[7]);  // AND_Gate
  assign xor_3_out = {8{IO}} ^ multiplexer_1_out;  // XOR_Gate xor_3, 8 bits wide
  and and_7 (CMPO, alu_rom_data[8], OE);
  assign bit_extender_1_out = {{7{OE}}, OE};  // Bit_Extender bit_extender_1
  assign ALUOUT = xor_3_out & bit_extender_1_out;  // AND_Gate and_8, 8 bits wide

  // Other names for the same wires on the sheet: OET = OE

  // Notes on the sheet:
  //   contents of alu_rom (hex, n*v repeats v):
  //   16*0 4 4 4*1 10*5 104 112 112 101 118 100 101 118 100 39*0 105 11f 107 104 101 114 111 11c 113 11e
  //   11b 10c 103 100 112 118 140 15a 120 180 12*105 16*0 4 4 4 6*1 7*0 4 1 1 4 1 1 4 1 1 4 1 1 4 1 1 0
  //   6*5 10*0 4 1 1 13*0 4 1 1
endmodule

module cu (
  input  [7:0] IRIN,
  input  IRI_IN,
  input  CLK,
  input  RESET,
  output [7:0] CUOUT,
  output [3:0] INFLAG,
  output [2:0] OUTFLAG,
  output PCC,
  output IRI_OUT
);

  wire decoder_1_out1, decoder_1_out2;
  wire [1:0] cuctr_q;
  wire [7:0] and_1_out, and_2_out, bit_extender_1_out, bit_extender_2_out, cu_rom_2_data, cu_rom_data;
  wire [7:7] or_1_out;

  Counter #(.max('h2), .trigger("falling"), .width(2)) cuctr (
    .clr(RESET), .load(1'b0), .up(1'b1), .count(1'b1), .clk(CLK), .D(2'b00), .Q(cuctr_q));  // open: carry
  Register register_1 (.D(IRIN), .en(IRI_IN), .clk(CLK), .Q(CUOUT), .clr(RESET));
  ROM cu_rom (.addr(CUOUT), .data(cu_rom_data));
  ROM cu_rom_2 (.addr(CUOUT), .data(cu_rom_2_data));
  Decoder #(.enable("false"), .select(2)) decoder_1 (
    .out0(IRI_OUT), .out1(decoder_1_out1), .out2(decoder_1_out2), .sel(cuctr_q));  // open: out3
  assign and_1_out = cu_rom_data & bit_extender_1_out;  // AND_Gate and_1, 8 bits wide
  assign bit_extender_1_out = {{7{decoder_1_out1}}, decoder_1_out1};  // Bit_Extender bit_extender_1
  assign and_2_out = cu_rom_2_data & bit_extender_2_out;  // AND_Gate and_2, 8 bits wide
  assign bit_extender_2_out = {{7{decoder_1_out2}}, decoder_1_out2};  // Bit_Extender bit_extender_2
  assign {or_1_out[7], OUTFLAG, INFLAG} = and_1_out | and_2_out;  // OR_Gate or_1, 8 bits wide
  or or_2 (PCC, or_1_out[7], IRI_OUT);

  // Notes on the sheet:
  //   contents of cu_rom (hex, n*v repeats v):
  //   48*0 11*80 5*0 11*80 53*0 23 23 23 33 33 33 43 43 43 53 53 53 7*0 23 33 43 53 53 53
  //   contents of cu_rom_2 (hex, n*v repeats v):
  //   16*0 25 26 34 26 44 45 10*0 20 20 40 20 20 0 40 40 8*0 11*f0 5*0 11*f0 5*0 32*34 d4 d5 d6 13*0 64 65
  //   66 64 65 66 64 65 66 64 65 66 4*0 22 32 42 22 32 42 22 32 42 23 33 43 4*0 14 15 16 13*0 21 31 41
  //   61*0 f
endmodule

module jmp (
  input  [7:0] JMPINS,
  input  OE,
  input  ZIN,
  input  OIN,
  input  CIN,
  input  SIN,
  input  [15:0] PCIN,
  input  [7:0] DATABUS,
  input  CLK,
  input  RESET,
  output PCOE,
  output [15:0] PCOUT
);

  wire bitselector_1_out;
  wire [4:0] jmp_rom_data;
  wire [7:0] HIGHBITS_q;
  wire [10:2] not_2_out;
  wire [15:0] adder_1_out;

  ROM #(.dataWidth(5)) jmp_rom (.addr(JMPINS), .data(jmp_rom_data));
  Register HIGHBITS (.D(DATABUS), .en(1'b1), .clk(CLK), .Q(HIGHBITS_q), .clr(RESET));
  or or_1 (not_2_out[4], ZIN, CIN);
  xor xor_1 (not_2_out[7], OIN, SIN);
  not not_1 (not_2_out[9], not_2_out[7]);
  not not_2 (not_2_out[2], ZIN);
  not not_3 (not_2_out[5], not_2_out[4]);
  not not_4 (not_2_out[6], CIN);
  or or_2 (not_2_out[8], ZIN, not_2_out[7]);
  and and_1 (not_2_out[10], not_2_out[9], ~ZIN);  // AND_Gate
  Adder #(.width(16)) adder_1 (.a(PCIN), .b({HIGHBITS_q, DATABUS}), .out(adder_1_out), .cin(1'b0));  // open: cout
  Multiplexer #(.enable("true"), .width(16)) multiplexer_1 (
    .in0({HIGHBITS_q, DATABUS}), .in1(adder_1_out), .out(PCOUT), .sel(jmp_rom_data[4]), .en(PCOE));
  and and_2 (PCOE, OE, bitselector_1_out);
  BitSelector #(.width(11)) bitselector_1 (
    .in({not_2_out[10:4], CIN, not_2_out[2], ZIN, 1'b1}), .out(bitselector_1_out), .sel(jmp_rom_data[3:0]));

  // Notes on the sheet:
  //   contents of jmp_rom (hex, n*v repeats v):
  //   49*0 1 2 3 4 5 6 7 8 9 a 6*0 11 12 13 14 15 16 17 18 19 1a
  //   =
  //   !=
  //   <
  //   <=
  //   >=
  //   < s
  //   > s
  //   >
  //   <= s
  //   >= s
endmodule

module cmp (
  input  [7:0] CMPIN,
  input  OVERFLOW,
  input  CARRY,
  input  OE,
  input  CLK,
  input  RESET,
  output ZFLAGO,
  output OFLAGO,
  output CFLAGO,
  output SFLAGO
);

  wire and_1_out, and_2_out, and_3_out, and_4_out, and_5_out, and_6_out, and_7_out, and_8_out, and_9_out;

  and and_1 (and_1_out, ~CMPIN[0], ~CMPIN[1], ~CMPIN[2], ~CMPIN[3], ~CMPIN[4], ~CMPIN[5], ~CMPIN[6], ~CMPIN[7]);  // AND_Gate
  S_R_Flip_Flop s_r_ff_1 (
    .S(and_2_out), .R(and_3_out), .clk(CLK), .Q(ZFLAGO), .reset(RESET), .preset(1'b0));  // open: Qn
  and and_2 (and_2_out, and_1_out, OE);
  and and_3 (and_3_out, ~and_1_out, OE);  // AND_Gate
  S_R_Flip_Flop s_r_ff_2 (
    .S(and_4_out), .R(and_5_out), .clk(CLK), .Q(OFLAGO), .reset(RESET), .preset(1'b0));  // open: Qn
  and and_4 (and_4_out, OVERFLOW, OE);
  and and_5 (and_5_out, ~OVERFLOW, OE);  // AND_Gate
  S_R_Flip_Flop s_r_ff_3 (
    .S(and_6_out), .R(and_7_out), .clk(CLK), .Q(CFLAGO), .reset(RESET), .preset(1'b0));  // open: Qn
  and and_6 (and_6_out, CARRY, OE);
  and and_7 (and_7_out, ~CARRY, OE);  // AND_Gate
  and and_8 (and_8_out, CMPIN[7], OE);
  and and_9 (and_9_out, ~CMPIN[7], OE);  // AND_Gate
  S_R_Flip_Flop s_r_ff_4 (
    .S(and_8_out), .R(and_9_out), .clk(CLK), .Q(SFLAGO), .reset(RESET), .preset(1'b0));  // open: Qn
endmodule

module computer (
  input  clk,
  output [7:0] computer_output
);

  main computer_main (.clk(clk), .input_pins({8{1'b0}}), .output_pins(computer_output));
endmodule
